# Fritzing sketch UnlockKidsZone (saved by Fritzing 0.9.3b)
breadboards: 1

parts:
  Part1 = Arduino Uno (Rev3)
  IR_Transmitter_Module = KY-005 Infrared Transmitter Module [package="Breakout board"]
  R1 = Resistor [tolerance=±5% resistance=330 package="2010 [SMD]"]

nets:
  N1: Part1.GND, R1.Pin_1
  N2: Part1.D3_PWM, IR_Transmitter_Module.S
  N3: IR_Transmitter_Module.-, R1.Pin_0

custom parts:
  KY-005 Infrared Transmitter Module: Arduino IR Transmitter Module Keyes KY-005, emits infrared light at 38KHz.
